// Logisim project r-s and gated latch.circ as structural Verilog: 1 circuit, main circuit main
module main (
  input  in_1,
  input  in_2,
  input  flip_to_store_1,
  input  flip_to_store_0,
  input  store,
  input  write_enable,
  output a,
  output a__storage,
  output b,
  output a__storage_2,
  output b_2
);

  wire and_1_out, nand_1_out, nand_2_out, not_2_out;

  and and_1 (and_1_out, in_1, in_2);
  not not_1 (a, and_1_out);
  nand nand_1 (nand_1_out, store, write_enable);
  nand nand_2 (nand_2_out, write_enable, not_2_out);
  not not_2 (not_2_out, store);
  nand nand_3 (a__storage, flip_to_store_1, b);
  nand nand_4 (b, a__storage, flip_to_store_0);
  nand nand_5 (a__storage_2, nand_1_out, b_2);
  nand nand_6 (b_2, a__storage_2, nand_2_out);

  // Notes on the sheet:
  //   keep one always on
  //   R-S Latch
  //   Gated D Latch
endmodule
