// Logisim project 2 bit and 4 bit adder.circ as structural Verilog: 1 circuit, main circuit main
module main (
  input  A,
  input  B,
  input  C,
  input  C_2,
  input  in_5,
  input  in_6,
  input  in_7,
  input  in_8,
  input  in_9,
  input  in_10,
  input  in_11,
  input  in_12,
  output carry,
  output s,
  output out_15,
  output out_16,
  output out_17,
  output out_18,
  output carry_2
);

  wire and_2_out, and_3_out, and_4_out, and_5_out, and_6_out, and_7_out, and_8_out, and_10_out, and_11_out,
       and_13_out, and_14_out, and_15_out, and_16_out, and_18_out, and_19_out, and_21_out, and_22_out,
       and_23_out, and_24_out, and_26_out, and_27_out, and_28_out, and_29_out, and_30_out, and_31_out,
       and_32_out, and_34_out, and_35_out, and_37_out, and_38_out, and_39_out, and_40_out, not_1_out,
       not_2_out, not_3_out, not_4_out, not_5_out, not_6_out, not_7_out, not_8_out, not_9_out, not_10_out,
       not_11_out, not_12_out, not_13_out, not_14_out, not_15_out, not_16_out, not_17_out, not_18_out,
       not_19_out, not_20_out, not_21_out, not_22_out, not_23_out, not_24_out, not_25_out, not_26_out,
       not_27_out, not_28_out, not_29_out, not_30_out, not_31_out, not_32_out, not_33_out, not_34_out,
       not_35_out, not_36_out, not_37_out, not_38_out, not_39_out, not_40_out, not_41_out, not_42_out,
       not_43_out, not_44_out, not_45_out, not_46_out, not_47_out, not_48_out, not_49_out, not_50_out,
       not_51_out, not_52_out, not_53_out, not_54_out, not_55_out, not_56_out, not_57_out, not_58_out,
       not_59_out, not_60_out, or_1_out, or_3_out, or_5_out;

  not not_1 (not_1_out, in_5);
  not not_2 (not_2_out, in_9);
  not not_3 (not_3_out, C_2);
  not not_4 (not_4_out, in_5);
  not not_5 (not_5_out, in_9);
  not not_6 (not_6_out, in_5);
  not not_7 (not_7_out, C_2);
  not not_8 (not_8_out, in_5);
  not not_9 (not_9_out, in_9);
  not not_10 (not_10_out, C_2);
  not not_11 (not_11_out, in_9);
  not not_12 (not_12_out, C_2);
  // AND_Gate and_1 has open pins: in0=not_1_out, in2=not_2_out, in4=not_3_out, out=open
  and and_2 (and_2_out, not_4_out, not_5_out, C_2);
  and and_3 (and_3_out, not_6_out, in_9, not_7_out);
  and and_4 (and_4_out, not_8_out, in_9, C_2);
  and and_5 (and_5_out, in_5, not_9_out, not_10_out);
  and and_6 (and_6_out, in_5, not_11_out, C_2);
  and and_7 (and_7_out, in_5, in_9, not_12_out);
  and and_8 (and_8_out, in_5, in_9, C_2);
  or or_1 (or_1_out, and_4_out, and_6_out, and_7_out, and_8_out);
  or or_2 (out_15, and_8_out, and_2_out, and_3_out, and_5_out);
  not not_13 (not_13_out, in_6);
  // AND_Gate and_9 has open pins: in0=not_13_out, in2=not_14_out, in4=not_15_out, out=open
  not not_14 (not_14_out, in_10);
  not not_15 (not_15_out, or_1_out);
  not not_16 (not_16_out, in_6);
  not not_17 (not_17_out, in_10);
  and and_10 (and_10_out, not_16_out, not_17_out, or_1_out);
  not not_18 (not_18_out, in_6);
  and and_11 (and_11_out, not_18_out, in_10, not_19_out);
  not not_19 (not_19_out, or_1_out);
  not not_20 (not_20_out, in_6);
  and and_12 (and_11_out, not_20_out, in_10, or_1_out);
  and and_13 (and_13_out, in_6, not_21_out, not_22_out);
  not not_21 (not_21_out, in_10);
  not not_22 (not_22_out, or_1_out);
  and and_14 (and_14_out, in_6, not_23_out, or_1_out);
  not not_23 (not_23_out, in_10);
  and and_15 (and_15_out, in_6, in_10, not_24_out);
  not not_24 (not_24_out, or_1_out);
  and and_16 (and_16_out, in_6, in_10, or_1_out);
  or or_3 (or_3_out, and_11_out, and_14_out, and_15_out, and_16_out);
  or or_4 (out_16, and_16_out, and_10_out, and_11_out, and_13_out);
  not not_25 (not_25_out, in_7);
  not not_26 (not_26_out, in_11);
  not not_27 (not_27_out, or_3_out);
  not not_28 (not_28_out, in_7);
  not not_29 (not_29_out, in_11);
  not not_30 (not_30_out, in_7);
  not not_31 (not_31_out, or_3_out);
  not not_32 (not_32_out, in_7);
  not not_33 (not_33_out, in_11);
  not not_34 (not_34_out, or_3_out);
  not not_35 (not_35_out, in_11);
  not not_36 (not_36_out, or_3_out);
  // AND_Gate and_17 has open pins: in0=not_25_out, in2=not_26_out, in4=not_27_out, out=open
  and and_18 (and_18_out, not_28_out, not_29_out, or_3_out);
  and and_19 (and_19_out, not_30_out, in_11, not_31_out);
  and and_20 (and_19_out, not_32_out, in_11, or_3_out);
  and and_21 (and_21_out, in_7, not_33_out, not_34_out);
  and and_22 (and_22_out, in_7, not_35_out, or_3_out);
  and and_23 (and_23_out, in_7, in_11, not_36_out);
  and and_24 (and_24_out, in_7, in_11, or_3_out);
  or or_5 (or_5_out, and_19_out, and_22_out, and_23_out, and_24_out);
  or or_6 (out_17, and_24_out, and_18_out, and_19_out, and_21_out);
  not not_37 (not_37_out, A);
  // AND_Gate and_25 has open pins: in0=not_37_out, in2=not_38_out, in4=not_39_out, out=open
  not not_38 (not_38_out, B);
  not not_39 (not_39_out, C);
  not not_40 (not_40_out, A);
  and and_26 (and_26_out, not_40_out, not_41_out, C);
  not not_41 (not_41_out, B);
  not not_42 (not_42_out, A);
  and and_27 (and_27_out, not_42_out, B, not_43_out);
  not not_43 (not_43_out, C);
  not not_44 (not_44_out, A);
  and and_28 (and_28_out, not_44_out, B, C);
  and and_29 (and_29_out, A, not_45_out, not_46_out);
  not not_45 (not_45_out, B);
  not not_46 (not_46_out, C);
  and and_30 (and_30_out, A, not_47_out, C);
  not not_47 (not_47_out, B);
  and and_31 (and_31_out, A, B, not_48_out);
  not not_48 (not_48_out, C);
  and and_32 (and_32_out, A, B, C);
  or or_7 (carry, and_28_out, and_30_out, and_31_out, and_32_out);
  or or_8 (s, and_32_out, and_26_out, and_27_out, and_29_out);
  not not_49 (not_49_out, in_8);
  not not_50 (not_50_out, in_12);
  // AND_Gate and_33 has open pins: in0=not_49_out, in2=not_50_out, in4=not_51_out, out=open
  not not_51 (not_51_out, or_5_out);
  not not_52 (not_52_out, in_8);
  not not_53 (not_53_out, in_12);
  and and_34 (and_34_out, not_52_out, not_53_out, or_5_out);
  not not_54 (not_54_out, in_8);
  and and_35 (and_35_out, not_54_out, in_12, not_55_out);
  not not_55 (not_55_out, or_5_out);
  not not_56 (not_56_out, in_8);
  and and_36 (and_35_out, not_56_out, in_12, or_5_out);
  not not_57 (not_57_out, in_12);
  and and_37 (and_37_out, in_8, not_57_out, not_58_out);
  not not_58 (not_58_out, or_5_out);
  and and_38 (and_38_out, in_8, not_59_out, or_5_out);
  not not_59 (not_59_out, in_12);
  and and_39 (and_39_out, in_8, in_12, not_60_out);
  not not_60 (not_60_out, or_5_out);
  and and_40 (and_40_out, in_8, in_12, or_5_out);
  or or_9 (carry_2, and_35_out, and_38_out, and_39_out, and_40_out);
  or or_10 (out_18, and_40_out, and_34_out, and_35_out, and_37_out);

  // Notes on the sheet:
  //   8 bit adder
  //   2 bit adder
endmodule
