// Logisim project decoder.circ as structural Verilog: 1 circuit, main circuit main
module main (
  input  in_1,
  input  in_2,
  output out_3,
  output out_4,
  output out_5,
  output out_6
);

  wire not_1_out, not_2_out, not_3_out, not_4_out;

  not not_1 (not_1_out, in_1);
  and and_1 (out_3, not_1_out, not_2_out);
  not not_2 (not_2_out, in_2);
  not not_3 (not_3_out, in_1);
  and and_2 (out_4, not_3_out, in_2);
  and and_3 (out_5, in_1, not_4_out);
  not not_4 (not_4_out, in_2);
  and and_4 (out_6, in_1, in_2);
endmodule
