// Logisim project multiplexer.circ as structural Verilog: 1 circuit, main circuit main
module main (
  input  A,
  input  B,
  input  S__secondary,
  input  in_4,
  input  A_2,
  input  B_2,
  input  C,
  input  D,
  input  S1,
  input  S0,
  input  in_11
);

  wire and_1_out, and_2_out, and_3_out, and_4_out, and_5_out, and_6_out, not_1_out, not_2_out, not_3_out,
       not_4_out, not_5_out;

  not not_1 (not_1_out, S__secondary);
  and and_1 (and_1_out, A, not_1_out);
  or or_1 (in_4, and_1_out, and_3_out);
  not not_2 (not_2_out, S1);
  not not_3 (not_3_out, S0);
  and and_2 (and_2_out, A_2, not_2_out, not_3_out);
  and and_3 (and_3_out, B, S__secondary);
  not not_4 (not_4_out, S1);
  and and_4 (and_4_out, B_2, not_4_out, S0);
  or or_2 (in_11, and_2_out, and_4_out, and_5_out, and_6_out);
  not not_5 (not_5_out, S0);
  and and_5 (and_5_out, C, S1, not_5_out);
  and and_6 (and_6_out, D, S1, S0);

  // Notes on the sheet:
  //   Multiplexer. Selects one of the inputs and connects it to the output.
endmodule
