// Logisim project nor and or gates.circ as structural Verilog: 1 circuit, main circuit main
module main (
  input  in,
  input  in_2,
  input  in_3,
  input  in_4,
  output out,
  output out_2
);

  wire transistor_1_out, transistor_3_out, transistor_4_out, transistor_5_out, transistor_6_out,
       transistor_7_out, transistor_8_out, transistor_10_out;

  Transistor transistor_1 (.in(1'b1), .out(transistor_1_out), .gate(in));
  Transistor transistor_2 (.in(transistor_1_out), .out(out), .gate(in_2));
  Transistor #(.\type ("n")) transistor_3 (.in(out), .out(transistor_3_out), .gate(in_2));
  Transistor transistor_4 (.in(1'b1), .out(transistor_4_out), .gate(in_3));
  Transistor transistor_5 (.in(transistor_4_out), .out(transistor_5_out), .gate(in_4));
  Transistor #(.\type ("n")) transistor_6 (.in(transistor_5_out), .out(transistor_6_out), .gate(in_4));
  Transistor #(.\type ("n")) transistor_7 (.in(out), .out(transistor_7_out), .gate(in));
  Transistor #(.\type ("n")) transistor_8 (.in(transistor_5_out), .out(transistor_8_out), .gate(in_3));
  Transistor transistor_9 (.in(1'b1), .out(out_2), .gate(transistor_5_out));
  Transistor #(.\type ("n")) transistor_10 (.in(out_2), .out(transistor_10_out), .gate(transistor_5_out));
  // also tied to GND on the sheet: {transistor_3_out, transistor_6_out, transistor_7_out, transistor_8_out, transistor_10_out}
endmodule
