// Logisim project increasing complexity.circ as structural Verilog
module transistor_basics (
  input  source,
  input  source_2,
  input  gate,
  input  gate_2,
  input  source_3,
  input  source_4,
  input  gate_3,
  input  gate_4,
  output drain,
  output drain_2,
  output drain_3,
  output drain_4
);

  Transistor #(.\type ("n")) transistor_1 (.in(source), .out(drain), .gate(gate));
  Transistor #(.\type ("n")) transistor_2 (.in(source_3), .out(drain_3), .gate(gate_3));
  Pull_Resistor pull_resistor_1 (.node(drain));
  Pull_Resistor pull_resistor_2 (.node(drain_3));
  Transistor transistor_3 (.in(source_2), .out(drain_2), .gate(gate_2));
  Pull_Resistor pull_resistor_3 (.node(drain_2));
  Transistor transistor_4 (.in(source_4), .out(drain_4), .gate(gate_4));
  Pull_Resistor pull_resistor_4 (.node(drain_4));

  // Notes on the sheet:
  //   n-type transistor
  //   p-type transistor
endmodule

module not__transistors (
  input  in,
  output out
);

  Transistor transistor_1 (.in(1'b1), .out(out), .gate(in));
  Transistor #(.\type ("n")) transistor_2 (.in(1'b0), .out(out), .gate(in));

  // Notes on the sheet:
  //   in: pull=down
  //   out: pull=up
  //   not gate: reverses input
endmodule

module \not  (
  input  in,
  output out
);

  not__transistors \not  (.in(in), .out(out));

  // Notes on the sheet:
  //   not gate: reverses input
endmodule

module nor__transistors (
  input  a,
  input  b,
  output out
);

  wire transistor_1_out;

  Transistor transistor_1 (.in(1'b1), .out(transistor_1_out), .gate(a));
  Transistor transistor_2 (.in(transistor_1_out), .out(out), .gate(b));
  Transistor #(.\type ("n")) transistor_3 (.in(1'b0), .out(out), .gate(b));
  Transistor #(.\type ("n")) transistor_4 (.in(1'b0), .out(out), .gate(a));
  Pull_Resistor pull_resistor_1 (.node(transistor_1_out));

  // Notes on the sheet:
  //   nor: if any input, no output
endmodule

module or__transistors (
  input  a,
  input  b,
  output out
);

  wire transistor_1_out, transistor_2_out;

  Transistor #(.\type ("n")) transistor_1 (.in(1'b0), .out(transistor_1_out), .gate(b));
  Transistor transistor_2 (.in(1'b1), .out(transistor_2_out), .gate(a));
  Pull_Resistor pull_resistor_1 (.node(transistor_2_out));
  Transistor transistor_3 (.in(transistor_2_out), .out(transistor_1_out), .gate(b));
  Transistor #(.\type ("n")) transistor_4 (.in(1'b0), .out(transistor_1_out), .gate(a));
  Transistor transistor_5 (.in(1'b1), .out(out), .gate(transistor_1_out));
  Transistor #(.\type ("n")) transistor_6 (.in(1'b0), .out(out), .gate(transistor_1_out));

  // Notes on the sheet:
  //   out: pull=up
  //   nor: if any input, no output
  //   or: if one or both inputs is active, output
  //   not gate: reverses input
endmodule

module \or  (
  input  a,
  input  b,
  output out
);

  wire nor_out;

  nor__transistors \nor  (.a(a), .b(b), .out(nor_out));
  not__transistors \not  (.in(nor_out), .out(out));

  // Notes on the sheet:
  //   or: if one or both inputs is active, output
endmodule

module nand__transistors (
  input  a,
  input  b,
  output out
);

  wire transistor_2_out, transistor_3_out;

  Transistor transistor_1 (.in(1'b1), .out(out), .gate(a));
  Transistor #(.\type ("n")) transistor_2 (.in(out), .out(transistor_2_out), .gate(a));
  Pull_Resistor pull_resistor_1 (.node(transistor_2_out));
  Transistor #(.\type ("n")) transistor_3 (.in(transistor_2_out), .out(transistor_3_out), .gate(b));
  Transistor transistor_4 (.in(1'b1), .out(out), .gate(b));
  Pull_Resistor pull_resistor_2 (.node(out));
  // also tied to GND on the sheet: transistor_3_out

  // Notes on the sheet:
  //   out: pull=up
  //   nand: does not turn off unless both inputs triggered
endmodule

module and__transistors (
  input  a,
  input  b,
  output out
);

  wire transistor_1_out, transistor_3_out, transistor_4_out;

  Transistor transistor_1 (.in(1'b1), .out(transistor_1_out), .gate(a));
  Transistor transistor_2 (.in(1'b1), .out(transistor_1_out), .gate(b));
  Transistor #(.\type ("n")) transistor_3 (.in(transistor_1_out), .out(transistor_3_out), .gate(a));
  Pull_Resistor pull_resistor_1 (.node(transistor_3_out));
  Transistor #(.\type ("n")) transistor_4 (.in(transistor_3_out), .out(transistor_4_out), .gate(b));
  Pull_Resistor pull_resistor_2 (.node(transistor_1_out));
  Transistor transistor_5 (.in(1'b1), .out(out), .gate(transistor_1_out));
  Transistor #(.\type ("n")) transistor_6 (.in(1'b0), .out(out), .gate(transistor_1_out));
  // also tied to GND on the sheet: transistor_4_out

  // Notes on the sheet:
  //   out: pull=up
  //   nand: does not turn off unless both inputs triggered
  //   and: only output if both inputs are triggered
  //   not gate: reverses input
endmodule

module \and  (
  input  a,
  input  b,
  output out
);

  wire nand_out;

  nand__transistors \nand  (.a(a), .b(b), .out(nand_out));
  not__transistors \not  (.in(nand_out), .out(out));

  // Notes on the sheet:
  //   and: only output if both inputs are triggered
endmodule

module not_and_or_with_nand (
  input  a,
  input  b,
  output \not ,
  output out_4,
  output \and ,
  output out_6,
  output \or ,
  output out_8
);

  wire nand_2_out, nand_3_out, nand_5_out, nand_6_out;

  not not_1 (\not , a);
  nand nand_1 (out_4, a, a);
  and and_1 (\and , a, b);
  nand nand_2 (nand_2_out, a, b);
  nand nand_3 (nand_3_out, a, b);
  nand nand_4 (out_6, nand_3_out, nand_2_out);
  or or_1 (\or , a, b);
  nand nand_5 (nand_5_out, a, a);
  nand nand_6 (nand_6_out, b, b);
  nand nand_7 (out_8, nand_5_out, nand_6_out);
endmodule

module decoder__2_input (
  input  a,
  input  b,
  output w,
  output x,
  output y,
  output z
);

  wire not_2_out, not_3_out, not_4_out, not_out;

  \not  \not  (.in(a), .out(not_out));
  \not  not_2 (.in(b), .out(not_2_out));
  \not  not_3 (.in(a), .out(not_3_out));
  \not  not_4 (.in(b), .out(not_4_out));
  and__transistors \and  (.a(not_out), .b(not_2_out), .out(w));
  and__transistors and_2 (.a(not_3_out), .b(b), .out(x));
  and__transistors and_3 (.a(a), .b(not_4_out), .out(y));
  and__transistors and_4 (.a(a), .b(b), .out(z));

  // Notes on the sheet:
  //   decoder: exactly one output is 1 depending on inputs
endmodule

module decoder__3_input (
  input  a,
  input  b,
  input  c,
  output s,
  output v,
  output t,
  output u,
  output x,
  output y,
  output w,
  output z
);

  wire not_1_out, not_2_out, not_3_out, not_4_out, not_5_out, not_6_out, not_7_out, not_8_out, not_9_out,
       not_10_out, not_11_out, not_12_out;

  not not_1 (not_1_out, a);
  not not_2 (not_2_out, b);
  and and_1 (s, not_1_out, not_2_out, not_3_out);
  not not_3 (not_3_out, c);
  not not_4 (not_4_out, a);
  and and_2 (v, not_4_out, not_5_out, c);
  not not_5 (not_5_out, b);
  not not_6 (not_6_out, b);
  and and_3 (t, a, not_6_out, not_7_out);
  not not_7 (not_7_out, c);
  not not_8 (not_8_out, a);
  and and_4 (u, not_8_out, b, not_9_out);
  not not_9 (not_9_out, c);
  not not_10 (not_10_out, a);
  and and_5 (x, not_10_out, b, c);
  and and_6 (y, a, not_11_out, c);
  not not_11 (not_11_out, b);
  and and_7 (w, a, b, not_12_out);
  not not_12 (not_12_out, c);
  and and_8 (z, a, b, c);

  // Notes on the sheet:
  //   decoder: exactly one output is 1 depending on inputs
endmodule

module mux__2_to_1 (
  input  selector,
  input  a,
  input  b,
  output out
);

  wire and_1_out, and_2_out, not_1_out;

  not not_1 (not_1_out, selector);
  and and_1 (and_1_out, not_1_out, a);
  and and_2 (and_2_out, selector, b);
  or or_1 (out, and_1_out, and_2_out);

  // Notes on the sheet:
  //   mux: selects an input to connect to the output
  //   off selects a
  //   on selects b
endmodule

module mux__4_to_1 (
  input  s2,
  input  s1,
  input  d,
  input  c,
  input  b,
  input  a,
  output out
);

  wire and_1_out, and_2_out, and_3_out, and_4_out, not_1_out, not_2_out, not_3_out, not_4_out;

  not not_1 (not_1_out, s1);
  not not_2 (not_2_out, s2);
  not not_3 (not_3_out, s1);
  not not_4 (not_4_out, s2);
  and and_1 (and_1_out, d, s1, s2);
  and and_2 (and_2_out, c, not_1_out, s2);
  and and_3 (and_3_out, b, s1, not_2_out);
  and and_4 (and_4_out, a, not_3_out, not_4_out);
  or or_1 (out, and_1_out, and_2_out, and_3_out, and_4_out);

  // Notes on the sheet:
  //   mux: connect a certain input to one specified output
endmodule

module adder__2_bit (
  input  a,
  input  b,
  input  carry_in,
  output carry_out,
  output decimal_out
);

  wire and_1_out, and_2_out, and_3_out, and_4_out, and_5_out, and_6_out, and_7_out, and_8_out, not_1_out,
       not_2_out, not_3_out, not_4_out, not_5_out, not_6_out, not_7_out, not_8_out, not_9_out, not_10_out,
       not_11_out, not_12_out;

  not not_1 (not_1_out, a);
  not not_2 (not_2_out, b);
  not not_3 (not_3_out, carry_in);
  not not_4 (not_4_out, a);
  not not_5 (not_5_out, b);
  not not_6 (not_6_out, a);
  not not_7 (not_7_out, carry_in);
  not not_8 (not_8_out, a);
  not not_9 (not_9_out, b);
  not not_10 (not_10_out, carry_in);
  not not_11 (not_11_out, b);
  not not_12 (not_12_out, carry_in);
  and and_1 (and_1_out, not_1_out, not_2_out, not_3_out);
  and and_2 (and_2_out, not_4_out, not_5_out, carry_in);
  and and_3 (and_3_out, not_6_out, b, not_7_out);
  and and_4 (and_4_out, not_8_out, b, carry_in);
  and and_5 (and_5_out, a, not_9_out, not_10_out);
  and and_6 (and_6_out, a, not_11_out, carry_in);
  and and_7 (and_7_out, a, b, not_12_out);
  and and_8 (and_8_out, a, b, carry_in);
  or or_1 (carry_out, and_4_out, and_6_out, and_7_out, and_8_out);
  or or_2 (decimal_out, and_8_out, and_2_out, and_3_out, and_5_out);

  // Notes on the sheet:
  //   8 bit adder
endmodule

module adder__8_bit (
  input  in_1,
  input  a1,
  input  a2,
  input  a4,
  input  a8,
  input  a16,
  input  a32,
  input  a64,
  input  a128,
  input  b1,
  input  b2,
  input  b4,
  input  b8,
  input  b16,
  input  b32,
  input  b64,
  input  b128,
  output o1,
  output o2,
  output o4,
  output o8,
  output o16,
  output o32,
  output o64,
  output o128,
  output carry_out_256
);

  wire adder_2_bit_1_carry_out, adder_2_bit_2_carry_out, adder_2_bit_3_carry_out, adder_2_bit_4_carry_out,
       adder_2_bit_5_carry_out, adder_2_bit_6_carry_out, adder_2_bit_7_carry_out;

  adder__2_bit adder_2_bit_1 (.a(a1), .b(b1), .carry_in(in_1), .carry_out(adder_2_bit_1_carry_out), .decimal_out(o1));
  adder__2_bit adder_2_bit_2 (
    .a(a2), .b(b2), .carry_in(adder_2_bit_1_carry_out), .carry_out(adder_2_bit_2_carry_out), .decimal_out(o2));
  adder__2_bit adder_2_bit_3 (
    .a(a4), .b(b4), .carry_in(adder_2_bit_2_carry_out), .carry_out(adder_2_bit_3_carry_out), .decimal_out(o4));
  adder__2_bit adder_2_bit_4 (
    .a(a8), .b(b8), .carry_in(adder_2_bit_3_carry_out), .carry_out(adder_2_bit_4_carry_out), .decimal_out(o8));
  adder__2_bit adder_2_bit_5 (
    .a(a16), .b(b16), .carry_in(adder_2_bit_4_carry_out), .carry_out(adder_2_bit_5_carry_out),
    .decimal_out(o16));
  adder__2_bit adder_2_bit_6 (
    .a(a32), .b(b32), .carry_in(adder_2_bit_5_carry_out), .carry_out(adder_2_bit_6_carry_out),
    .decimal_out(o32));
  adder__2_bit adder_2_bit_7 (
    .a(a64), .b(b64), .carry_in(adder_2_bit_6_carry_out), .carry_out(adder_2_bit_7_carry_out),
    .decimal_out(o64));
  adder__2_bit adder_2_bit_8 (
    .a(a128), .b(b128), .carry_in(adder_2_bit_7_carry_out), .carry_out(carry_out_256), .decimal_out(o128));

  // Notes on the sheet:
  //   initial carry in generally 0
endmodule

module adder_subtracter__4_bit (
  input  a4,
  input  a3,
  input  a2,
  input  a1,
  input  b4,
  input  b3,
  input  b2,
  input  b1,
  input  _0_1__selector,
  output carry_out,
  output c4,
  output c3,
  output c2,
  output c1
);

  wire adder_2_bit_1_carry_out, adder_2_bit_2_carry_out, adder_2_bit_3_carry_out, mux_2_to_1_1_out,
       mux_2_to_1_2_out, mux_2_to_1_3_out, mux_out, not_1_out, not_2_out, not_3_out, not_4_out;

  not not_1 (not_1_out, b3);
  not not_2 (not_2_out, b4);
  mux__2_to_1 mux (.a(b4), .b(not_2_out), .selector(_0_1__selector), .out(mux_out));
  adder__2_bit adder (.a(a4), .b(mux_out), .carry_in(adder_2_bit_1_carry_out), .carry_out(carry_out), .decimal_out(c4));
  not not_3 (not_3_out, b2);
  mux__2_to_1 mux_2_to_1_1 (.a(b3), .b(not_1_out), .selector(_0_1__selector), .out(mux_2_to_1_1_out));
  mux__2_to_1 mux_2_to_1_2 (.a(b2), .b(not_3_out), .selector(_0_1__selector), .out(mux_2_to_1_2_out));
  adder__2_bit adder_2_bit_1 (
    .a(a3), .b(mux_2_to_1_1_out), .carry_in(adder_2_bit_2_carry_out), .carry_out(adder_2_bit_1_carry_out),
    .decimal_out(c3));
  adder__2_bit adder_2_bit_2 (
    .a(a2), .b(mux_2_to_1_2_out), .carry_in(adder_2_bit_3_carry_out), .carry_out(adder_2_bit_2_carry_out),
    .decimal_out(c2));
  not not_4 (not_4_out, b1);
  mux__2_to_1 mux_2_to_1_3 (.a(b1), .b(not_4_out), .selector(_0_1__selector), .out(mux_2_to_1_3_out));
  adder__2_bit adder_2_bit_3 (
    .a(a1), .b(mux_2_to_1_3_out), .carry_in(_0_1__selector), .carry_out(adder_2_bit_3_carry_out),
    .decimal_out(c1));
endmodule

module and_or_latch (
  input  d,
  input  reset,
  output q
);

  wire not_1_out, or_1_out;

  or or_1 (or_1_out, q, d);
  not not_1 (not_1_out, reset);
  and and_1 (q, or_1_out, not_1_out);

  // Notes on the sheet:
  //   and-or latch: stores a single bit of information
endmodule

module gated_latch (
  input  d,
  input  we,
  output q
);

  wire and_1_out, and_2_out, not_1_out, not_2_out, or_1_out;

  and and_1 (and_1_out, d, we);
  not not_1 (not_1_out, d);
  and and_2 (and_2_out, not_1_out, we);
  or or_1 (or_1_out, q, and_1_out);
  not not_2 (not_2_out, and_2_out);
  and and_3 (q, or_1_out, not_2_out);

  // Notes on the sheet:
  //   gated latch: allows us to store a single bit of information when write enabled is on
  //   and-or latch: stores a single bit of information
endmodule

module r_s_latch (
  input  s,
  input  r,
  output store
);

  wire and_1_out, and_2_out, not_2_out;

  not not_1 (store, and_1_out);
  and and_1 (and_1_out, s, not_2_out);
  not not_2 (not_2_out, and_2_out);
  and and_2 (and_2_out, store, r);

  // Notes on the sheet:
  //   quiescent state: both r and s at 1
  //   keep one on always to avoid errors
  //   flipping one results in storing its value
endmodule

module gated_d_latch (
  input  store,
  input  write_enable,
  output stored
);

  wire and_1_out, and_2_out, not_1_out, not_2_out, not_3_out;

  not not_1 (not_1_out, store);
  not not_2 (not_2_out, and_1_out);
  and and_1 (and_1_out, store, write_enable);
  not not_3 (not_3_out, and_2_out);
  and and_2 (and_2_out, write_enable, not_1_out);
  r_s_latch r_s_latch (.s(not_2_out), .r(not_3_out), .store(stored));
endmodule

module gated_d_latch__with_full_r_s_latch (
  input  store,
  input  write_enable,
  output stored
);

  wire and_1_out, and_2_out, and_3_out, and_4_out, not_1_out, not_2_out, not_3_out, not_5_out;

  not not_1 (not_1_out, store);
  not not_2 (not_2_out, and_1_out);
  and and_1 (and_1_out, store, write_enable);
  not not_3 (not_3_out, and_2_out);
  and and_2 (and_2_out, write_enable, not_1_out);
  and and_3 (and_3_out, not_2_out, not_5_out);
  and and_4 (and_4_out, stored, not_3_out);
  not not_4 (stored, and_3_out);
  not not_5 (not_5_out, and_4_out);

  // Notes on the sheet:
  //   store: pull=up
  //   write_enable: pull=up
  //   stored: pull=up
endmodule

module register__4_bit__gated_d_latch (
  input  store_1,
  input  store_2,
  input  store_4,
  input  store_8,
  input  write_enable,
  output stored_1,
  output stored_2,
  output stored_4,
  output stored_8
);

  gated_d_latch__with_full_r_s_latch gated_d_latch_with_full_r_s_latch_1 (
    .store(store_1), .write_enable(write_enable), .stored(stored_1));
  gated_d_latch__with_full_r_s_latch gated_d_latch_with_full_r_s_latch_2 (
    .store(store_2), .write_enable(write_enable), .stored(stored_2));
  gated_d_latch__with_full_r_s_latch gated_d_latch_with_full_r_s_latch_3 (
    .store(store_4), .write_enable(write_enable), .stored(stored_4));
  gated_d_latch__with_full_r_s_latch gated_d_latch_with_full_r_s_latch_4 (
    .store(store_8), .write_enable(write_enable), .stored(stored_8));

  // Notes on the sheet:
  //   (flip write enable to clear errors)
  //   register: store a 4 bit value
endmodule

module register__8_bit__gated_latch (
  input  e,
  input  d0,
  input  d1,
  input  d2,
  input  d3,
  input  d4,
  input  d5,
  input  d6,
  input  d7,
  output q0,
  output q1,
  output q2,
  output q3,
  output q4,
  output q5,
  output q6,
  output q7
);

  gated_latch gated_latch_1 (.d(d0), .we(e), .q(q0));
  gated_latch gated_latch_2 (.d(d1), .we(e), .q(q1));
  gated_latch gated_latch_3 (.d(d2), .we(e), .q(q2));
  gated_latch gated_latch_4 (.d(d3), .we(e), .q(q3));
  gated_latch gated_latch_5 (.d(d4), .we(e), .q(q4));
  gated_latch gated_latch_6 (.d(d5), .we(e), .q(q5));
  gated_latch gated_latch_7 (.d(d6), .we(e), .q(q6));
  gated_latch gated_latch_8 (.d(d7), .we(e), .q(q7));

  // Notes on the sheet:
  //   write enable
  //   8 bit storage
  //   gated latches
endmodule

module memory_bit (
  input  column,
  input  row,
  input  d,
  input  we,
  input  re,
  output q
);

  wire and_1_out, and_2_out, and_3_out, gated_latch_1_q;

  and and_1 (and_1_out, row, column);
  and and_2 (and_2_out, we, and_1_out);
  gated_latch gated_latch_1 (.d(d), .we(and_2_out), .q(gated_latch_1_q));
  Transistor #(.\type ("n"), .gate("br")) transistor_1 (.in(gated_latch_1_q), .out(q), .gate(and_3_out));
  and and_3 (and_3_out, and_1_out, re);
endmodule
