// Logisim project lc-3.circ as structural Verilog
module adder__1_bit (
  input  bit_a_in,
  input  bit_b_in,
  input  bit_carry_in,
  output bit_carry,
  output bit_result
);

  wire and_1_out, and_2_out, and_3_out, and_4_out, and_5_out, and_6_out, and_7_out, and_8_out, not_1_out,
       not_2_out, not_3_out, not_4_out, not_5_out, not_6_out, not_7_out, not_8_out, not_9_out, not_10_out,
       not_11_out, not_12_out;

  and and_1 (and_1_out, bit_a_in, bit_b_in, bit_carry_in);
  and and_2 (and_2_out, bit_a_in, bit_b_in, not_2_out);
  not not_1 (not_1_out, bit_b_in);
  not not_2 (not_2_out, bit_carry_in);
  and and_3 (and_3_out, bit_a_in, not_1_out, bit_carry_in);
  not not_3 (not_3_out, bit_a_in);
  not not_4 (not_4_out, bit_carry_in);
  not not_5 (not_5_out, bit_b_in);
  and and_4 (and_4_out, bit_a_in, not_5_out, not_4_out);
  or or_1 (bit_result, and_1_out, and_4_out, and_6_out, and_7_out);
  not not_6 (not_6_out, bit_a_in);
  and and_5 (and_5_out, not_3_out, bit_b_in, bit_carry_in);
  and and_6 (and_6_out, not_6_out, bit_b_in, not_8_out);
  not not_7 (not_7_out, bit_b_in);
  not not_8 (not_8_out, bit_carry_in);
  not not_9 (not_9_out, bit_a_in);
  and and_7 (and_7_out, not_9_out, not_7_out, bit_carry_in);
  not not_10 (not_10_out, bit_a_in);
  not not_11 (not_11_out, bit_b_in);
  not not_12 (not_12_out, bit_carry_in);
  and and_8 (and_8_out, not_10_out, not_11_out, not_12_out);
  or or_2 (bit_carry, and_5_out, and_3_out, and_2_out, and_1_out);

  // Notes on the sheet:
  //   adder (1 bit)
  //   Add two 1 bit sequences and a potential carry together. Output their sum by a result and a carry bit.
endmodule

module adder__2_bit (
  input  [1:0] _2_bit_a,
  input  [1:0] _2_bit_b,
  input  carry_bit_in,
  output carry_bit_out,
  output [1:0] _2_bit_result
);

  wire adder_1_bit_1_bit_carry;

  adder__1_bit adder_1_bit_1 (
    .bit_carry_in(carry_bit_in), .bit_carry(adder_1_bit_1_bit_carry), .bit_a_in(_2_bit_a[1]),
    .bit_b_in(_2_bit_b[1]), .bit_result(_2_bit_result[1]));
  adder__1_bit adder_1_bit_2 (
    .bit_carry_in(adder_1_bit_1_bit_carry), .bit_carry(carry_bit_out), .bit_a_in(_2_bit_a[0]),
    .bit_b_in(_2_bit_b[0]), .bit_result(_2_bit_result[0]));
endmodule

module adder__4_bit (
  input  [3:0] _4_bit_a,
  input  [3:0] _4_bit_b,
  input  carry_bit_in,
  output carry_bit_out,
  output [3:0] _4_bit_result
);

  wire adder_2_bit_1_carry_bit_out;

  adder__2_bit adder_2_bit_1 (
    .carry_bit_in(carry_bit_in), ._2_bit_a(_4_bit_a[3:2]), ._2_bit_b(_4_bit_b[3:2]),
    ._2_bit_result(_4_bit_result[3:2]), .carry_bit_out(adder_2_bit_1_carry_bit_out));
  adder__2_bit adder_2_bit_2 (
    .carry_bit_in(adder_2_bit_1_carry_bit_out), ._2_bit_a(_4_bit_a[1:0]), ._2_bit_b(_4_bit_b[1:0]),
    ._2_bit_result(_4_bit_result[1:0]), .carry_bit_out(carry_bit_out));
endmodule

module adder__8_bit (
  input  [7:0] _8_bit_a,
  input  [7:0] _8_bit_b,
  input  carry_bit_in,
  output carry_bit_out,
  output [7:0] _8_bit_result
);

  wire adder_4_bit_1_carry_bit_out;

  adder__4_bit adder_4_bit_1 (
    .carry_bit_in(carry_bit_in), ._4_bit_a(_8_bit_a[7:4]), ._4_bit_b(_8_bit_b[7:4]),
    ._4_bit_result(_8_bit_result[7:4]), .carry_bit_out(adder_4_bit_1_carry_bit_out));
  adder__4_bit adder_4_bit_2 (
    .carry_bit_in(adder_4_bit_1_carry_bit_out), ._4_bit_a(_8_bit_a[3:0]), ._4_bit_b(_8_bit_b[3:0]),
    ._4_bit_result(_8_bit_result[3:0]), .carry_bit_out(carry_bit_out));
endmodule

module adder__16_bit (
  input  [15:0] _16_bit_a,
  input  [15:0] _16_bit_b,
  input  carry_bit_in,
  output carry_bit_out,
  output [15:0] _16_bit_result
);

  wire adder_8_bit_1_carry_bit_out;

  adder__8_bit adder_8_bit_1 (
    .carry_bit_in(carry_bit_in), ._8_bit_a(_16_bit_a[15:8]), ._8_bit_b(_16_bit_b[15:8]),
    ._8_bit_result(_16_bit_result[15:8]), .carry_bit_out(adder_8_bit_1_carry_bit_out));
  adder__8_bit adder_8_bit_2 (
    .carry_bit_in(adder_8_bit_1_carry_bit_out), ._8_bit_a(_16_bit_a[7:0]), ._8_bit_b(_16_bit_b[7:0]),
    ._8_bit_result(_16_bit_result[7:0]), .carry_bit_out(carry_bit_out));
endmodule

module adder__16_bit__1_bit_adders (
  input  [15:0] _16_bit_a,
  input  [15:0] _16_bit_b,
  input  carry_bit_in,
  output carry_bit_out,
  output [15:0] _16_bit_result
);

  wire adder_1_bit_1_bit_carry, adder_1_bit_2_bit_carry, adder_1_bit_3_bit_carry, adder_1_bit_4_bit_carry,
       adder_1_bit_5_bit_carry, adder_1_bit_6_bit_carry, adder_1_bit_7_bit_carry, adder_1_bit_8_bit_carry,
       adder_1_bit_9_bit_carry, adder_1_bit_10_bit_carry, adder_1_bit_11_bit_carry, adder_1_bit_12_bit_carry,
       adder_1_bit_13_bit_carry, adder_1_bit_14_bit_carry, adder_1_bit_15_bit_carry;

  adder__1_bit adder_1_bit_1 (
    .bit_carry_in(carry_bit_in), .bit_carry(adder_1_bit_1_bit_carry), .bit_a_in(_16_bit_a[15]),
    .bit_b_in(_16_bit_b[15]), .bit_result(_16_bit_result[15]));
  adder__1_bit adder_1_bit_2 (
    .bit_carry_in(adder_1_bit_3_bit_carry), .bit_carry(adder_1_bit_2_bit_carry), .bit_a_in(_16_bit_a[13]),
    .bit_b_in(_16_bit_b[13]), .bit_result(_16_bit_result[13]));
  adder__1_bit adder_1_bit_3 (
    .bit_carry_in(adder_1_bit_1_bit_carry), .bit_carry(adder_1_bit_3_bit_carry), .bit_a_in(_16_bit_a[14]),
    .bit_b_in(_16_bit_b[14]), .bit_result(_16_bit_result[14]));
  adder__1_bit adder_1_bit_4 (
    .bit_carry_in(adder_1_bit_2_bit_carry), .bit_carry(adder_1_bit_4_bit_carry), .bit_a_in(_16_bit_a[12]),
    .bit_b_in(_16_bit_b[12]), .bit_result(_16_bit_result[12]));
  adder__1_bit adder_1_bit_5 (
    .bit_carry_in(adder_1_bit_4_bit_carry), .bit_carry(adder_1_bit_5_bit_carry), .bit_a_in(_16_bit_a[11]),
    .bit_b_in(_16_bit_b[11]), .bit_result(_16_bit_result[11]));
  adder__1_bit adder_1_bit_6 (
    .bit_carry_in(adder_1_bit_7_bit_carry), .bit_carry(adder_1_bit_6_bit_carry), .bit_a_in(_16_bit_a[9]),
    .bit_b_in(_16_bit_b[9]), .bit_result(_16_bit_result[9]));
  adder__1_bit adder_1_bit_7 (
    .bit_carry_in(adder_1_bit_5_bit_carry), .bit_carry(adder_1_bit_7_bit_carry), .bit_a_in(_16_bit_a[10]),
    .bit_b_in(_16_bit_b[10]), .bit_result(_16_bit_result[10]));
  adder__1_bit adder_1_bit_8 (
    .bit_carry_in(adder_1_bit_6_bit_carry), .bit_carry(adder_1_bit_8_bit_carry), .bit_a_in(_16_bit_a[8]),
    .bit_b_in(_16_bit_b[8]), .bit_result(_16_bit_result[8]));
  adder__1_bit adder_1_bit_9 (
    .bit_carry_in(adder_1_bit_8_bit_carry), .bit_carry(adder_1_bit_9_bit_carry), .bit_a_in(_16_bit_a[7]),
    .bit_b_in(_16_bit_b[7]), .bit_result(_16_bit_result[7]));
  adder__1_bit adder_1_bit_10 (
    .bit_carry_in(adder_1_bit_11_bit_carry), .bit_carry(adder_1_bit_10_bit_carry), .bit_a_in(_16_bit_a[5]),
    .bit_b_in(_16_bit_b[5]), .bit_result(_16_bit_result[5]));
  adder__1_bit adder_1_bit_11 (
    .bit_carry_in(adder_1_bit_9_bit_carry), .bit_carry(adder_1_bit_11_bit_carry), .bit_a_in(_16_bit_a[6]),
    .bit_b_in(_16_bit_b[6]), .bit_result(_16_bit_result[6]));
  adder__1_bit adder_1_bit_12 (
    .bit_carry_in(adder_1_bit_10_bit_carry), .bit_carry(adder_1_bit_12_bit_carry), .bit_a_in(_16_bit_a[4]),
    .bit_b_in(_16_bit_b[4]), .bit_result(_16_bit_result[4]));
  adder__1_bit adder_1_bit_13 (
    .bit_carry_in(adder_1_bit_12_bit_carry), .bit_carry(adder_1_bit_13_bit_carry), .bit_a_in(_16_bit_a[3]),
    .bit_b_in(_16_bit_b[3]), .bit_result(_16_bit_result[3]));
  adder__1_bit adder_1_bit_14 (
    .bit_carry_in(adder_1_bit_13_bit_carry), .bit_carry(adder_1_bit_14_bit_carry), .bit_a_in(_16_bit_a[2]),
    .bit_b_in(_16_bit_b[2]), .bit_result(_16_bit_result[2]));
  adder__1_bit adder_1_bit_15 (
    .bit_carry_in(adder_1_bit_14_bit_carry), .bit_carry(adder_1_bit_15_bit_carry), .bit_a_in(_16_bit_a[1]),
    .bit_b_in(_16_bit_b[1]), .bit_result(_16_bit_result[1]));
  adder__1_bit adder_1_bit_16 (
    .bit_carry_in(adder_1_bit_15_bit_carry), .bit_carry(carry_bit_out), .bit_a_in(_16_bit_a[0]),
    .bit_b_in(_16_bit_b[0]), .bit_result(_16_bit_result[0]));
endmodule

module ander__16_bit (
  input  [15:0] _16_bit_a,
  input  [15:0] _16_bit_b,
  output [15:0] _16_bit_result
);

  and and_1 (_16_bit_result[15], _16_bit_a[15], _16_bit_b[15]);
  and and_2 (_16_bit_result[14], _16_bit_a[14], _16_bit_b[14]);
  and and_3 (_16_bit_result[12], _16_bit_a[12], _16_bit_b[12]);
  and and_4 (_16_bit_result[13], _16_bit_a[13], _16_bit_b[13]);
  and and_5 (_16_bit_result[11], _16_bit_a[11], _16_bit_b[11]);
  and and_6 (_16_bit_result[10], _16_bit_a[10], _16_bit_b[10]);
  and and_7 (_16_bit_result[9], _16_bit_a[9], _16_bit_b[9]);
  and and_8 (_16_bit_result[8], _16_bit_a[8], _16_bit_b[8]);
  and and_9 (_16_bit_result[6], _16_bit_a[6], _16_bit_b[6]);
  and and_10 (_16_bit_result[7], _16_bit_a[7], _16_bit_b[7]);
  and and_11 (_16_bit_result[4], _16_bit_a[4], _16_bit_b[4]);
  and and_12 (_16_bit_result[5], _16_bit_a[5], _16_bit_b[5]);
  and and_13 (_16_bit_result[2], _16_bit_a[2], _16_bit_b[2]);
  and and_14 (_16_bit_result[3], _16_bit_a[3], _16_bit_b[3]);
  and and_15 (_16_bit_result[1], _16_bit_a[1], _16_bit_b[1]);
  and and_16 (_16_bit_result[0], _16_bit_a[0], _16_bit_b[0]);

  // Notes on the sheet:
  //   ander (16 bit)
  //   Performs the AND operation on two 16 bit binary numbers.
endmodule

module notter__16_bit (
  input  [15:0] _16_bit_a,
  output [15:0] _16_bit_result
);

  not not_1 (_16_bit_result[9], _16_bit_a[9]);
  not not_2 (_16_bit_result[13], _16_bit_a[13]);
  not not_3 (_16_bit_result[12], _16_bit_a[12]);
  not not_4 (_16_bit_result[14], _16_bit_a[14]);
  not not_5 (_16_bit_result[15], _16_bit_a[15]);
  not not_6 (_16_bit_result[11], _16_bit_a[11]);
  not not_7 (_16_bit_result[10], _16_bit_a[10]);
  not not_8 (_16_bit_result[2], _16_bit_a[2]);
  not not_9 (_16_bit_result[8], _16_bit_a[8]);
  not not_10 (_16_bit_result[3], _16_bit_a[3]);
  not not_11 (_16_bit_result[5], _16_bit_a[5]);
  not not_12 (_16_bit_result[4], _16_bit_a[4]);
  not not_13 (_16_bit_result[1], _16_bit_a[1]);
  not not_14 (_16_bit_result[6], _16_bit_a[6]);
  not not_15 (_16_bit_result[7], _16_bit_a[7]);
  not not_16 (_16_bit_result[0], _16_bit_a[0]);

  // Notes on the sheet:
  //   notter (16 bit)
  //   Performs the NOT operation on a 16 bit binary number.
endmodule
